# Fritzing sketch CPEN_291_P2_hand_wiring (saved by Fritzing 0.9.10b)
breadboards: 1

parts:
  Pico_H1 = Raspberry Pi Pico H
  C1 = Ceramic Capacitor [capacitance=100nF voltage=35V package="100 mil [THT, multilayer]"]
  C2 = Ceramic Capacitor [capacitance=1µF voltage=35V package="100 mil [THT, multilayer]"]
  IC1 = Voltage Regulator [package=to-220-alt]
  SW1 = DIP SWITCH [package=dipswitch-02]
  VCC1 = Battery block 9V
  J1 = Basic Servo
  J2 = Basic Servo
  J3 = Basic Servo

nets:
  N1: Pico_H1.VSYS, C1.0, IC1.OUT
  GND: Pico_H1.GND, C2.1, IC1.IN, VCC1.-, J1.gnd, J2.gnd, J3.gnd
  VCC: Pico_H1.3V3, J1.vcc, J2.vcc, J3.vcc
  N2: Pico_H1.GP22, J3.pulse
  N3: Pico_H1.GP3, J2.pulse
  N4: Pico_H1.GP2, J1.pulse
  N5: C2.0, IC1.GND, SW1.3
  N6: SW1.2, VCC1.+

custom parts:
  Raspberry Pi Pico H: Raspberry Pi Pico H. Based around the RP2040 microcontroller the Pico H is a low cost microcontroller device bringing Raspberry Pi quality, cost, and easy of use to the microcontroller space.
